# Fritzing sketch arduinoUno (saved by Fritzing 0.9.3b)
breadboards: 1

parts:
  부품1 = Arduino Uno (Rev3)
  Piezo_Buzzer = Piezo Speaker
  part = LED - 5mm [color="Red (633nm)" package="5 mm [THT]"]
  Ultrasonic_Sensors = hc-sr04
  SW = Pushbutton [package="[SMD]"]
  part_2 = Resistor [tolerance=±5% resistance=220 package=THT]
  part_3 = Resistor [tolerance=±5% resistance=220 package=THT]
  Motion_Sensor = HC-SR501 Body Sensor Module
  part_4 = LED - 5mm [color="Yellow (595nm)" package="5 mm [THT]"]
  part_5 = Resistor [tolerance=±10% resistance=220 package=THT]
  Humidity_&_Temperature_Sensor = KY-015 Temperature & Humidity Sensor Module [package="Breakout board"]
  DC_Moter = DC Motor
  part_6 = LED - 5mm [color="Yellow (595nm)" package="5 mm [THT]"]
  part_7 = Resistor [tolerance=±10% resistance=220 package=THT]
  BT1 = Bluetooth HC-06u [package=THT]

nets:
  N1: 부품1.D8, Piezo_Buzzer.pin1
  N2: 부품1.D9_PWM, DC_Moter.pin_1
  N3: 부품1.D10_PWM/SS, Humidity_&_Temperature_Sensor.S
  N4: 부품1.D11_PWM/MOSI, Motion_Sensor.OUT
  N5: 부품1.D12/MISO, Ultrasonic_Sensors.Echo
  N6: 부품1.D13/SCK, Ultrasonic_Sensors.Trig
  GND: 부품1.GND, Piezo_Buzzer.pin2, Ultrasonic_Sensors.GND, SW.Pin_1, SW.Pin_2, part_3.Pin_1, Motion_Sensor.GND, part_4.cathode, Humidity_&_Temperature_Sensor.-, DC_Moter.pin_2, part_7.Pin_0, BT1.GND
  N7: 부품1.D2, BT1.RXD
  N8: 부품1.D3_PWM, BT1.TXD
  N9: 부품1.D4, part.anode
  N10: 부품1.D5_PWM, part_6.cathode
  N11: 부품1.D6_PWM, part_5.Pin_0
  N12: 부품1.D7, SW.Pin_3, SW.Pin_4, part_2.Pin_1
  N13: 부품1.3V3, part_2.Pin_0
  VCC: 부품1.5V, Ultrasonic_Sensors.VCC, Motion_Sensor.VCC, Humidity_&_Temperature_Sensor.Vin, BT1.VCC
  N14: part.cathode, part_3.Pin_0
  N15: part_4.anode, part_5.Pin_1
  N16: part_6.anode, part_7.Pin_1

custom parts:
  HC-SR501 Body Sensor Module: Pyroelectric Infrared PIR Motion Sensor Detector Module
  KY-015 Temperature & Humidity Sensor Module: KY-015 temperature and humidity sensor module, provides a low-latency serial interface to measure humidity and temperature.
  Bluetooth HC-06u: Bluetooth HC-06 - face up, pins down 16.5mm x 37.5mm PCB
