# Fritzing sketch 아두이노 메가 회로도 (saved by Fritzing 0.9.3b)
breadboards: 1

parts:
  부품1 = Arduino Mega 2560 (Rev3)
  LED1 = RGB LED (com. cathode, rgb) [package="5 mm [THT]"]
  R1 = Resistor [tolerance=±5% resistance=220 package=THT]
  LED2 = RGB LED (com. cathode, rgb) [package="5 mm [THT]"]
  R2 = Resistor [tolerance=±5% resistance=220 package=THT]
  LED3 = RGB LED (com. cathode, rgb) [package="5 mm [THT]"]
  R3 = Resistor [tolerance=±5% resistance=220 package=THT]
  LED4 = RGB LED (com. cathode, rgb) [package="5 mm [THT]"]
  R4 = Resistor [tolerance=±5% resistance=220 package=THT]
  R5 = Resistor [tolerance=±5% resistance=220 package=THT]
  R6 = Resistor [tolerance=±5% resistance=220 package=THT]
  R7 = Resistor [tolerance=±5% resistance=220 package=THT]
  R8 = Resistor [tolerance=±5% resistance=220 package=THT]
  R9 = PHOTOCELL [package=photocell-kit]
  LED5 = smd LED [color="Red (633nm)" package="0805 [SMD]"]
  LED6 = smd LED [color="Red (633nm)" package="0805 [SMD]"]
  R10 = Resistor [tolerance=±5% resistance=220 package=THT]
  R11 = Resistor [tolerance=±5% resistance=220 package=THT]
  J1 = Basic Servo
  S5 = Pushbutton [package="[THT]"]
  S6 = Pushbutton [package="[THT]"]
  S7 = Pushbutton [package="[THT]"]
  S8 = Pushbutton [package="[THT]"]
  S9 = Pushbutton [package="[THT]"]
  R12 = Resistor [tolerance=±5% resistance=220 package=THT]
  U1 = Graphical LCD 128x64 [package=lcd-g12864]
  R13 = TRIMPOT [package=trimpot-3mm]
  BT2 = Bluetooth HC-06u [package=THT]

nets:
  N1: 부품1.A0, R9.P$1, R10.Pin_0, BT2.VCC
  N2: 부품1.D15/RX3, BT2.TXD
  N3: 부품1.D14/TX3, BT2.RXD
  GND: 부품1.GND, R2.Pin_1, R3.Pin_1, R4.Pin_1, R9.P$2, LED6.cathode, J1.gnd, S5.Pin_2, S6.Pin_2, S8.Pin_1, S8.Pin_2, S9.Pin_2, U1.DB2, U1.RST, U1.E, R13.CCW, BT2.GND
  N4: 부품1.D12_PWM, U1.DB3
  N5: 부품1.D11_PWM, U1.DB1
  N6: 부품1.D8_PWM, U1.R_W
  N7: 부품1.IOREF, R5.Pin_1, R6.Pin_1, R7.Pin_1, R8.Pin_1, R10.Pin_1, J1.vcc, S5.Pin_3, S5.Pin_4, S6.Pin_3, S6.Pin_4, S7.Pin_3, S7.Pin_4, S8.Pin_3, S8.Pin_4, S9.Pin_3, S9.Pin_4, R12.Pin_1, U1.K, R13.CW
  N8: 부품1.D2_PWM, U1.VEE
  N9: 부품1.D3_PWM, U1.CS1
  N10: 부품1.D4_PWM, U1.DB0
  N11: 부품1.D22, R11.Pin_1
  N12: 부품1.D23, R5.Pin_0
  N13: 부품1.D25, LED1.red_anode
  N14: 부품1.D26, J1.pulse
  N15: 부품1.D27, LED1.green_anode
  N16: 부품1.D28, R12.Pin_0
  N17: 부품1.D29, LED1.blue_anode
  N18: 부품1.D30, R8.Pin_0
  N19: 부품1.D33, LED2.red_anode
  N20: 부품1.D34, LED4.blue_anode
  N21: 부품1.D37, LED2.green_anode
  N22: 부품1.D38, LED4.green_anode
  N23: 부품1.D41, LED2.blue_anode
  N24: 부품1.D42, LED4.red_anode
  N25: 부품1.D45, R6.Pin_0
  N26: 부품1.D46, R7.Pin_0
  N27: 부품1.D49, LED3.red_anode
  N28: 부품1.D50, LED3.blue_anode
  N29: 부품1.D53, LED3.green_anode
  N30: LED1.common_cathode, R1.Pin_0
  N31: R1.Pin_1, S7.Pin_1, S7.Pin_2
  N32: LED2.common_cathode, R2.Pin_0
  N33: LED3.common_cathode, R3.Pin_0
  N34: LED4.common_cathode, R4.Pin_0
  N35: LED5.cathode, LED6.anode
  N36: LED5.anode, R11.Pin_0
  N37: U1.A, R13.WIPER

custom parts:
  Bluetooth HC-06u: Bluetooth HC-06 - face up, pins down 16.5mm x 37.5mm PCB
